# Fritzing sketch attiny-prog (saved by Fritzing 0.8.7b)
breadboards: 1

parts:
  U1 = attiny85 [package=dip]
  C3 = Capacitor Polarized [package=cpol-radial-10uf-25v]
  Nano1 = Arduino Nano v2.3

nets:
  N1: U1.Pin_1, Nano1.D10
  GND: U1.Pin_4, C3.+, Nano1.GND
  N2: U1.Pin_5, Nano1.D11
  N3: U1.Pin_6, Nano1.D12
  N4: U1.Pin_7, Nano1.D13
  N5: U1.Pin_8, Nano1.+5V
  N6: C3.-, Nano1.RST
