# Fritzing sketch nadajnik (saved by Fritzing 0.8.7b)

parts:
  U1 = attiny85 [package=dip]
  BAT1 = Battery Holders [package=battcom_20mm_pth]
  S1 = Pushbutton [package="[THT]"]
  S2 = Pushbutton [package="[THT]"]
  S3 = Pushbutton [package="[THT]"]
  R6 = Resistor [tolerance=±5% resistance=10k package=THT]
  R7 = Resistor [tolerance=±5% resistance=10k package=THT]
  R8 = Resistor [tolerance=±5% resistance=10k package=THT]
  HM-10 = Bluetooth HM-10

nets:
  N1: U1.Pin_2, S2.Pin_1, S2.Pin_2, R7.Pin_0
  N2: U1.Pin_3, S3.Pin_1, S3.Pin_2, R8.Pin_0
  GND: U1.Pin_4, BAT1.-, R6.Pin_1, R7.Pin_1, R8.Pin_1, HM-10.GND
  N3: U1.Pin_5, S1.Pin_1, S1.Pin_2, R6.Pin_0
  N4: U1.Pin_6, HM-10.TXD
  N5: U1.Pin_7, HM-10.RXD
  N6: U1.Pin_8, BAT1.+, S1.Pin_3, S1.Pin_4, S2.Pin_3, S3.Pin_3, S3.Pin_4, HM-10.VCC
