# Fritzing sketch odbiornik-schem (saved by Fritzing 0.8.7b)

parts:
  LED1 = smd LED [color="Green (570nm)" package="0805 [SMD]"]
  HM-10 = Bluetooth HM-10
  DIN2 = DIN-5 jack (MIDI) [package=THT]
  U4 = ESP 32 DEVKIT DOIT

nets:
  GND: LED1.cathode, HM-10.GND, DIN2.2
  D4: LED1.anode
  TX2: HM-10.RXD
  RX2: HM-10.TXD
  3V3: HM-10.VCC, DIN2.4
  D18: DIN2.5
  N1: U4.D35, U4.EN
